# Fritzing sketch ESP32+LORA+GPS+OLED (saved by Fritzing 0.9.4)

parts:
  MH-ET_Live_Minikit_for_ESP1 = MH-ET Live Minikit for ESP32
  GY-NEO6MV3 = SUP500F [package=sup500f]
  LoRa_Module1 = Ra-01 - LoRa Module SX1278 [part_number=SX1278]
  J1 = single row smd female pin header, 1 pin [form="♀ (female)" part_number=reset]
  J2 = single row smd female pin header, 1 pin [form="♀ (female)" part_number=DIO0]
  J3 = single row smd female pin header, 1 pin [form="♀ (female)" part_number="LORA CLK"]
  J4 = single row smd female pin header, 1 pin [form="♀ (female)" part_number=MISO]
  J5 = female pin header, 2 pins [form="♀ (female)" part_number="TX RX"]
  J6 = single row smd male pin header, 1 pin [form="♂ (male)" part_number=MOSI]
  S1 = Pushbutton [package="[SMD]"]
  OLED1 = OLED 128x64 I2C Monochrome Display
  Q1 = Basic FET P-Channel [package="TO220 [THT]"]
  U1 = RELAY [package=relay-g5q]
  JP1 = Jumper [package=sj_2s-no]
  part = female pin header, 1 pin [form="♀ (female)"]

nets:
  N1: MH-ET_Live_Minikit_for_ESP1.IO34, GY-NEO6MV3.TX-O, J5.pin2
  N2: MH-ET_Live_Minikit_for_ESP1.TMS, S1.Pin_3, S1.Pin_4
  N3: MH-ET_Live_Minikit_for_ESP1.IO26, LoRa_Module1.DIO0, J2.pin1
  N4: MH-ET_Live_Minikit_for_ESP1.IO18, LoRa_Module1.NSS, part.pin1
  N5: MH-ET_Live_Minikit_for_ESP1.IO19, LoRa_Module1.MISO, J4.pin1
  N6: MH-ET_Live_Minikit_for_ESP1.IO23, LoRa_Module1.RESET, J1.pin1
  N7: MH-ET_Live_Minikit_for_ESP1.IO5, LoRa_Module1.SCK, J3.pin1
  3.3V: MH-ET_Live_Minikit_for_ESP1.3.3V, GY-NEO6MV3.VCC, LoRa_Module1.3.3V, OLED1.VDD
  N8: MH-ET_Live_Minikit_for_ESP1.IO22, OLED1.SCK
  N9: MH-ET_Live_Minikit_for_ESP1.IO21, OLED1.SDA
  GND: MH-ET_Live_Minikit_for_ESP1.GND, GY-NEO6MV3.RX-I, LoRa_Module1.GND, S1.Pin_1, S1.Pin_2, OLED1.GND
  N10: MH-ET_Live_Minikit_for_ESP1.IO27, LoRa_Module1.MOSI, J6.pin1
  N11: MH-ET_Live_Minikit_for_ESP1.TDI, GY-NEO6MV3.GND, J5.pin1
  N12: MH-ET_Live_Minikit_for_ESP1.IO4, Q1.gate
  N13: Q1.drain, U1.NC
  N14: Q1.source, JP1.2
  N15: U1.COIL1, JP1.1

notes:
  NEO6M wire color ESP32
  TX yellow 34 RX
  RX orange 12 TX
  Service Button
  GPIO14 on D1 Mini
  GPIO38 on TBEAM
  128 x 64 OLED SSD1306
  OLED wire color ESP32
  SDA purple 21
  SCL blue 22
  +5V power
  GND
  LORA NSS
  LORA MOSI
  LORA MISO
  LORA CLK

custom parts:
  MH-ET Live Minikit for ESP32: MH-ET Live Minikit for ESP32 ( http://mh.nodebb.com/topic/8/mh-et-live-minikit-for-esp32/2/) PCB footprint is invalid.
  Ra-01 - LoRa Module SX1278: The Ra-01 LoRa Module featuring the SX1278 engine by Semtech. Module by AI-Thinker. Module (Ra-01) specifications from: https://www.banggood.com/Ra-01-Smart-Electronics-SX1278-LoRa-Spread-Spectrum-Wireless-Module-Ultra-Far-10KM-433M-p-1130769.html Description: Power supply: DC1.8-3.7V(3.3V) Chip: SX1278 Frequency: 433Mhz Operating temperature: -40~+85°C On Sheild Description (may vary by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
